# Fritzing sketch maket (saved by Fritzing 0.9.2b)
circuit board: 8.46667cm x 5.64444cm
breadboards: 2

parts:
  DTH11 = Humidity and Temperature Sensor RHT03
  R2 = Resistor [tolerance=±5% resistance=10k package=THT]
  R6 = Resistor [tolerance=±5% resistance=3.3k package=THT]
  R7 = Resistor [tolerance=±5% resistance=3.3k package=THT]
  Деталь2 = Arduino Mini (Rev5)
  resistors = Resistor [tolerance=±5% resistance=3.3k package=THT]
  R11 = Photocell (LDR) [package=THT]
  resistors_2 = Resistor [tolerance=±5% resistance=3.3k package=THT]
  R13 = Resistor [tolerance=±5% resistance=10k package=THT]
  R14 = Resistor [tolerance=±5% resistance=10k package=THT]
  R15 = Resistor [tolerance=±5% resistance=10k package=THT]
  R16 = Resistor [tolerance=±5% resistance=150 package=THT]
  BPM180 = Barometric Pressure Sensor - BMP085 Breakout
  U1 = Graphical LCD 128x64 [package=lcd-g12864]
  R17 = Resistor [tolerance=±5% resistance=1.8k package=THT]
  R18 = Resistor [tolerance=±5% resistance=1.8k package=THT]
  R19 = Resistor [tolerance=±5% resistance=1.8k package=THT]
  R20 = Resistor [tolerance=±5% resistance=1.8k package=THT]
  R21 = Resistor [tolerance=±5% resistance=1.8k package=THT]
  R22 = Resistor [tolerance=±5% resistance=3.3k package=THT]
  resistors1 = Resistor [tolerance=±5% resistance=3.3k package=THT]
  Деталь3 = Real Time Clock Module - DS1307 RTC Breakout Board
  Q1 = PHOTOTRANSISTOR REFLECTIVE OBJECT SENSOR [package=qrb1114-side]
  R23 = Resistor [tolerance=±5% resistance=510 package=THT]
  R24 = Resistor [tolerance=±5% resistance=10k package=THT]
  Q2 = PHOTOTRANSISTOR REFLECTIVE OBJECT SENSOR [package=qrb1114-side]
  R26 = Resistor [tolerance=±5% resistance=10k package=THT]
  R27 = Resistor [tolerance=±5% resistance=510 package=THT]
  J1 = Basic Force Sensing Resistor (FSR) [package=THT]
  U2 = GAS_SENSOR [package=mq-3]
  J2 = Piezo Speaker
  U3 = HIH-4030 [package=hih-4030]
  S1 = SWITCH-MOMENTARY-2 [package=tactile-pth]
  D1 = Diode [package=diode-1n4148]
  D2 = Diode [part_number=1n4148 package=diode-1n4148]
  D3 = Diode [package=diode-1n4148]  # not connected
  D4 = Diode [package=diode-1n4148]
  LED1 = RGB LED (com. cathode, rgb) [package="5 mm [THT]"]

nets (from the breadboard view):
  N1: DTH11.Vcc, R2.Pin_1
  N2: DTH11.Data-signal, R2.Pin_0, Деталь2.D9_PWM, R11.pin_0, Q1.A, Q1.E, Q2.A, Q2.E, S1.1, D4.A
  GND: DTH11.GND_2, R6.Pin_1, R7.Pin_1, Деталь2.GND, resistors.Pin_1, resistors_2.Pin_1, R13.Pin_0, BPM180.GND, U1.DB3, R22.Pin_1, resistors1.Pin_1, Деталь3.GND, R23.Pin_0, R24.Pin_0, R26.Pin_1, R27.Pin_1, U2.B1, J2.pin1, U3.GND, LED1.red_anode
  N3: R6.Pin_0, U1.VSS, R21.Pin_0
  N4: R7.Pin_0, U1.DB1, R18.Pin_0
  5V: Деталь2.5V, R14.Pin_1, R15.Pin_1, BPM180.VCC, Деталь3.5V, U2.A1, J2.pin2, U3.VCC
  N5: Деталь2.A3, Q2.C, R26.Pin_0
  N6: Деталь2.A1, J1.pin_1
  N7: Деталь2.A0, U3.OUT
  N8: Деталь2.D13, J1.pin_0
  N9: Деталь2.D12, LED1.blue_anode
  N10: Деталь2.D11_PWM, LED1.green_anode
  N11: Деталь2.A6, R11.pin_1, R13.Pin_1
  N12: Деталь2.A4, R14.Pin_0, BPM180.SDA, Деталь3.SDA
  N13: Деталь2.A7, Q1.C, R24.Pin_1
  N14: Деталь2.A5, R15.Pin_0, BPM180.SCL, Деталь3.SCL
  N15: resistors.Pin_0, U1.DB0, R19.Pin_0, resistors1.Pin_0
  N16: resistors_2.Pin_0, U1.DB2, R17.Pin_0
  N17: R16.Pin_0, U1.VDD
  N18: U1.VO, R20.Pin_0, R22.Pin_0
  N19: U1.DB4, D1.C
  N20: Q1.K, R23.Pin_1
  N21: Q2.K, R27.Pin_0
  N22: D1.A, D2.A

notes:
  SDA
  SCL
  VCC
  GND
  BMP180
  ARDUINO MINI PRO
  LED
  SCE
  RST
  D/C
  DN<MOSI>
  SCLK
  5110 lcd display
  TCRT5000
  ds1307
  AO
  MQ-9
  KY-012
  MEAS
  KY-026
  KY-016
  KY-004
  1n4148 x4 (diodes)
  green
  blue
